// Logisim project T8.circ as structural Verilog: 11 circuits, main circuit main
module main (
  input  in_1,
  input  in_2,
  output [7:0] out_3
);

  wire and_1_out, and_2_out, and_3_out, and_4_out, clk_divider_1_out_3, clk_divider_1_out_4, clock_1_out,
       control_unit_1_out_6, control_unit_1_out_7, control_unit_1_out_8, control_unit_1_out_9,
       control_unit_1_out_10, control_unit_1_out_11, control_unit_1_out_12, control_unit_1_out_13,
       control_unit_1_out_14, control_unit_1_out_16, control_unit_1_out_18, control_unit_1_out_20,
       control_unit_1_out_21, control_unit_1_out_22, control_unit_1_out_24, control_unit_1_out_26,
       control_unit_1_out_29, control_unit_1_out_30, control_unit_1_out_31, control_unit_1_out_32, not_1_out,
       or_1_out, or_2_out, or_3_out, or_4_out, or_5_out, or_6_out, or_7_out, or_8_out, or_9_out, or_10_out;
  wire [1:0] control_unit_1_out_17, control_unit_1_out_19;
  wire [3:0] control_unit_1_out_15;
  wire [5:0] arithmetic_logic_unit_1_out_13, flag_register_1_data_out;
  wire [7:0] control_unit_1_out_27, control_unit_1_out_28, multiplexer_1_out, multiplexer_2_out,
       multiplexer_3_out, multiplexer_4_out, program_counter_1_adress_out, program_pointer_1_data_out,
       rom_1_data, rx_register_1_data_out, rx_register_2_data_out, rx_register_3_data_out,
       rx_register_4_data_out, stack_pointer_1_out_5, undriven;

  Stack_Pointer stack_pointer_1 (
    .in_1(in_1), .in_2(control_unit_1_out_18), .in_3(control_unit_1_out_21), .out_5(stack_pointer_1_out_5),
    .in_4(control_unit_1_out_20));
  not not_1 (not_1_out, clk_divider_1_out_3);
  CLK_DivIder clk_divider_1 (.out_3(clk_divider_1_out_3), .in_1(clock_1_out), .in_2(in_1), .out_4(clk_divider_1_out_4));
  and and_1 (and_1_out, in_2, not_1_out);
  Clock clock_1 (.out(clock_1_out));
  Control_Unit control_unit_1 (
    .in_1(out_3), .in_2(clk_divider_1_out_4), .in_3(clock_1_out), .in_4(in_1), .in_5(clk_divider_1_out_3),
    .out_6(control_unit_1_out_6), .out_7(control_unit_1_out_7), .out_8(control_unit_1_out_8),
    .out_9(control_unit_1_out_9), .out_10(control_unit_1_out_10), .out_11(control_unit_1_out_11),
    .out_12(control_unit_1_out_12), .out_13(control_unit_1_out_13), .out_23(stack_pointer_1_out_5),
    .out_15(control_unit_1_out_15), .out_25(out_3), .out_17(control_unit_1_out_17),
    .out_19(control_unit_1_out_19), .out_24(control_unit_1_out_24), .out_26(control_unit_1_out_26),
    .out_27(control_unit_1_out_27), .out_28(control_unit_1_out_28), .out_30(control_unit_1_out_30),
    .out_29(control_unit_1_out_29), .out_31(control_unit_1_out_31), .out_32(control_unit_1_out_32),
    .out_20(control_unit_1_out_20), .out_22(control_unit_1_out_22), .out_16(control_unit_1_out_16),
    .out_14(control_unit_1_out_14), .out_18(control_unit_1_out_18), .out_21(control_unit_1_out_21));
  RAM ram_1 (
    .addr(stack_pointer_1_out_5), .we(control_unit_1_out_14), .oe(control_unit_1_out_16), .clk(clock_1_out),
    .data(out_3));
  or or_1 (or_1_out, and_2_out, and_3_out);
  and and_2 (and_2_out, control_unit_1_out_29, flag_register_1_data_out[5]);
  Ram_Adress_Register ram_adress_register_1 (
    .ADRESS_IN(out_3), .CLK(clock_1_out), .RST(in_1), .ADRESS_OUT(stack_pointer_1_out_5));  // open: WRT, READ
  or or_2 (or_2_out, control_unit_1_out_30, or_3_out);
  or or_3 (or_3_out, or_1_out, and_4_out);
  and and_3 (and_3_out, control_unit_1_out_31, flag_register_1_data_out[4]);
  and and_4 (and_4_out, control_unit_1_out_32, flag_register_1_data_out[0]);
  LED led_1 (.in(program_counter_1_adress_out[6]));
  LED led_2 (.in(program_counter_1_adress_out[7]));
  assign control_unit_1_out_28 = control_unit_1_out_20 ? undriven : 8'bz;  // Controlled_Buffer controlled_buffer_1
  LED led_3 (.in(program_counter_1_adress_out[2]));
  LED led_4 (.in(program_counter_1_adress_out[3]));
  LED led_5 (.in(program_counter_1_adress_out[5]));
  LED led_6 (.in(program_counter_1_adress_out[4]));
  Program_Counter program_counter_1 (
    .RST(in_1), .JUMP(or_2_out), .EN(and_1_out), .CLK(clock_1_out), .ADRESS_IN(control_unit_1_out_28),
    .ADRESS_OUT(program_counter_1_adress_out));
  Pull_Resistor pull_resistor_1 (.node(out_3[3]));
  Pull_Resistor pull_resistor_2 (.node(out_3[6]));
  Pull_Resistor pull_resistor_3 (.node(out_3[7]));
  Pull_Resistor pull_resistor_4 (.node(out_3[2]));
  Pull_Resistor pull_resistor_5 (.node(out_3[5]));
  Pull_Resistor pull_resistor_6 (.node(out_3[4]));
  LED led_7 (.in(program_counter_1_adress_out[0]));
  LED led_8 (.in(program_counter_1_adress_out[1]));
  or or_4 (or_4_out, control_unit_1_out_24, control_unit_1_out_6);
  Pull_Resistor pull_resistor_7 (.node(out_3[1]));
  Pull_Resistor pull_resistor_8 (.node(out_3[0]));
  or or_5 (or_5_out, control_unit_1_out_24, control_unit_1_out_26);
  or or_6 (or_6_out, control_unit_1_out_22, and_1_out);
  or or_7 (or_7_out, control_unit_1_out_22, control_unit_1_out_20);
  Rx_Register rx_register_1 (
    .DATA_IN(out_3), .WRT(or_4_out), .CLK(clock_1_out), .RST(in_1), .READ(control_unit_1_out_7),
    .DATA_OUT_2(out_3), .DATA_OUT(rx_register_1_data_out));
  Rx_Register rx_register_2 (
    .DATA_IN(out_3), .WRT(control_unit_1_out_8), .CLK(clock_1_out), .RST(in_1), .READ(control_unit_1_out_9),
    .DATA_OUT_2(out_3), .DATA_OUT(rx_register_2_data_out));
  Rx_Register rx_register_3 (
    .DATA_IN(out_3), .WRT(control_unit_1_out_10), .CLK(clock_1_out), .RST(in_1),
    .READ(control_unit_1_out_11), .DATA_OUT_2(out_3), .DATA_OUT(rx_register_3_data_out));
  Rx_Register rx_register_4 (
    .DATA_IN(out_3), .WRT(control_unit_1_out_12), .CLK(clock_1_out), .RST(in_1),
    .READ(control_unit_1_out_13), .DATA_OUT_2(out_3), .DATA_OUT(rx_register_4_data_out));
  or or_8 (or_8_out, or_5_out, control_unit_1_out_29);
  or or_9 (or_9_out, or_8_out, control_unit_1_out_31);
  Program_Pointer program_pointer_1 (
    .DATA_IN(program_counter_1_adress_out), .WRT(or_6_out), .CLK(clock_1_out), .RST(in_1),
    .READ(control_unit_1_out_20), .DATA_OUT(program_pointer_1_data_out));
  assign out_3 = or_7_out ? program_pointer_1_data_out : 8'bz;  // Controlled_Buffer controlled_buffer_2
  or or_10 (or_10_out, or_9_out, control_unit_1_out_32);
  Multiplexer #(.select(2), .width(8), .enable("false")) multiplexer_1 (
    .in0(rx_register_1_data_out), .in1(rx_register_2_data_out), .in2(rx_register_3_data_out),
    .in3(rx_register_4_data_out), .out(multiplexer_1_out), .sel(control_unit_1_out_17));
  Multiplexer #(.select(2), .width(8), .enable("false")) multiplexer_2 (
    .in0(rx_register_1_data_out), .in1(rx_register_2_data_out), .in2(rx_register_3_data_out),
    .in3(rx_register_4_data_out), .out(multiplexer_2_out), .sel(control_unit_1_out_19));
  assign out_3 = and_1_out ? rom_1_data : 8'bz;  // Controlled_Buffer controlled_buffer_3
  Multiplexer #(.width(8), .enable("false")) multiplexer_3 (
    .in0(multiplexer_2_out), .in1(control_unit_1_out_27), .out(multiplexer_3_out), .sel(control_unit_1_out_26));
  ROM rom_1 (.addr(program_counter_1_adress_out), .data(rom_1_data));
  Multiplexer #(.width(8), .enable("false")) multiplexer_4 (
    .in0(multiplexer_1_out), .in1(rx_register_1_data_out), .out(multiplexer_4_out),
    .sel(control_unit_1_out_26));
  Arithmetic_Logic_Unit arithmetic_logic_unit_1 (
    .in_1(flag_register_1_data_out[5]), .in_2(flag_register_1_data_out[4]), .in_3(multiplexer_4_out),
    .in_4(multiplexer_3_out), .in_5(control_unit_1_out_24), .in_6(control_unit_1_out_15),
    .out_7(arithmetic_logic_unit_1_out_13[5]), .out_8(arithmetic_logic_unit_1_out_13[4]), .out_12(out_3),
    .out_9(arithmetic_logic_unit_1_out_13[3]), .out_10(arithmetic_logic_unit_1_out_13[2]),
    .out_11(arithmetic_logic_unit_1_out_13[1]), .out_13(arithmetic_logic_unit_1_out_13[0]));
  Flag_Register flag_register_1 (
    .DATA_IN(arithmetic_logic_unit_1_out_13), .WRT(control_unit_1_out_24), .CLK(clock_1_out), .RST(in_1),
    .READ(or_10_out), .DATA_OUT(flag_register_1_data_out));

  // Notes on the sheet:
  //   contents of rom_1 (hex, n*v repeats v):
  //   90 80 0 0 a0 123*0 90
endmodule

module Program_Counter (
  input  RST,
  input  JUMP,
  input  EN,
  input  CLK,
  input  [7:0] ADRESS_IN,
  output [7:0] ADRESS_OUT
);

  wire [7:0] counter_1_q;

  Counter counter_1 (
    .clr(RST), .load(JUMP), .up(1'b1), .count(EN), .clk(CLK), .D(ADRESS_IN), .Q(counter_1_q));  // open: carry
  assign ADRESS_OUT = EN ? counter_1_q : 8'bz;  // Controlled_Buffer controlled_buffer_1
endmodule

module Ram_Adress_Register (
  input  [7:0] ADRESS_IN,
  input  WRT,
  input  CLK,
  input  RST,
  input  READ,
  output [7:0] ADRESS_OUT
);

  wire [7:0] register_1_q;

  Register register_1 (.D(ADRESS_IN), .en(WRT), .clk(CLK), .Q(register_1_q), .clr(RST));
  assign ADRESS_OUT = READ ? register_1_q : 8'bz;  // Controlled_Buffer controlled_buffer_1
endmodule

module Rx_Register (
  input  [7:0] DATA_IN,
  input  WRT,
  input  CLK,
  input  RST,
  input  READ,
  output [7:0] DATA_OUT,
  output [7:0] DATA_OUT_2
);

  Register register_1 (.D(DATA_IN), .en(WRT), .clk(CLK), .Q(DATA_OUT), .clr(RST));
  assign DATA_OUT_2 = READ ? DATA_OUT : 8'bz;  // Controlled_Buffer controlled_buffer_1
endmodule

module Instructuon_Register (
  input  [7:0] INST_IN,
  input  WRT,
  input  CLK,
  input  RST,
  input  READ,
  output [15:0] INST_OUT
);

  wire not_1_out;
  wire [7:0] register_1_q, register_2_q;

  Register register_1 (.D(INST_IN), .en(WRT), .clk(CLK), .Q(register_1_q), .clr(RST));
  Register register_2 (.D(register_1_q), .en(WRT), .clk(CLK), .Q(register_2_q), .clr(RST));
  assign INST_OUT = READ ? {register_2_q, register_1_q} : 16'bz;  // Controlled_Buffer controlled_buffer_1
  not not_1 (not_1_out, READ);
  assign INST_OUT = not_1_out ? {16{1'b0}} : 16'bz;  // Controlled_Buffer controlled_buffer_2
endmodule

module CLK_DivIder (
  input  in_1,
  input  in_2,
  output out_3,
  output out_4
);

  wire t_ff_1_q;

  T_Flip_Flop t_ff_1 (.T(1'b1), .clk(in_1), .Q(t_ff_1_q), .reset(in_2));  // open: Qn, preset
  T_Flip_Flop t_ff_2 (.T(t_ff_1_q), .clk(in_1), .Q(out_3), .reset(in_2));  // open: Qn, preset
  not not_1 (out_4, out_3);
endmodule

module Control_Unit (
  input  [7:0] in_1,
  input  in_2,
  input  in_3,
  input  in_4,
  input  in_5,
  output out_6,
  output out_7,
  output out_8,
  output out_9,
  output out_10,
  output out_11,
  output out_12,
  output out_13,
  output out_14,
  output [3:0] out_15,
  output out_16,
  output [1:0] out_17,
  output out_18,
  output [1:0] out_19,
  output out_20,
  output out_21,
  output out_22,
  output [7:0] out_23,
  output out_24,
  output [7:0] out_25,
  output out_26,
  output [7:0] out_27,
  output [7:0] out_28,
  output out_29,
  output out_30,
  output out_31,
  output out_32
);

  wire and_1_out, and_3_out, and_5_out, and_7_out, and_9_out, and_10_out, and_11_out, and_12_out, and_13_out,
       and_14_out, d_ff_2_q, decoder_1_out0, decoder_1_out1, decoder_1_out2, decoder_1_out3, decoder_2_out0,
       decoder_2_out1, decoder_2_out2, decoder_2_out3, decoder_2_out5, not_1_out, or_1_out, or_2_out,
       or_8_out, or_9_out, or_10_out, or_12_out, or_13_out, or_15_out, or_16_out, or_18_out;
  wire [7:0] instructuon_register_1_inst_out;
  wire [15:8] instructuon_register_1_inst_out_2;

  Instructuon_Register instructuon_register_1 (
    .INST_IN(in_1), .WRT(in_2), .CLK(in_3), .RST(in_4), .READ(in_5),
    .INST_OUT({instructuon_register_1_inst_out_2, instructuon_register_1_inst_out}));
  or or_1 (or_1_out, decoder_2_out1, decoder_2_out2);
  assign out_23 = or_1_out ? instructuon_register_1_inst_out : 8'bz;  // Controlled_Buffer controlled_buffer_1
  Decoder #(.select(2), .enable("false")) decoder_1 (
    .out0(decoder_1_out0), .out1(decoder_1_out1), .out2(decoder_1_out2), .out3(decoder_1_out3),
    .sel(instructuon_register_1_inst_out_2[9:8]));
  Decoder #(.select(4), .enable("false")) decoder_2 (
    .out0(decoder_2_out0), .out1(decoder_2_out1), .out2(decoder_2_out2), .out3(decoder_2_out3),
    .out4(out_26), .out5(decoder_2_out5), .out6(out_29), .out7(out_31), .out8(out_32), .out9(out_20),
    .out10(out_22), .sel(instructuon_register_1_inst_out_2[15:12]));  // open: out11, out12, out13, out14, out15
  and and_1 (and_1_out, decoder_2_out1, decoder_1_out0);
  and and_2 (out_7, decoder_2_out2, decoder_1_out0);
  and and_3 (and_3_out, decoder_2_out1, decoder_1_out1);
  and and_4 (out_9, decoder_2_out2, decoder_1_out1);
  and and_5 (and_5_out, decoder_2_out1, decoder_1_out2);
  and and_6 (out_11, decoder_2_out2, decoder_1_out2);
  and and_7 (and_7_out, decoder_2_out1, decoder_1_out3);
  and and_8 (out_13, decoder_2_out2, decoder_1_out3);
  or or_2 (or_2_out, out_20, decoder_2_out5);
  and and_9 (and_9_out, decoder_1_out0, decoder_2_out3);
  and and_10 (and_10_out, decoder_1_out1, decoder_2_out3);
  and and_11 (and_11_out, decoder_1_out2, decoder_2_out3);
  and and_12 (and_12_out, decoder_1_out3, decoder_2_out3);
  or or_3 (out_30, or_2_out, out_22);
  or or_4 (out_6, and_1_out, and_9_out);
  or or_5 (out_8, and_10_out, and_3_out);
  or or_6 (out_10, and_11_out, and_5_out);
  or or_7 (out_12, and_7_out, and_12_out);
  assign out_15 = or_8_out ? instructuon_register_1_inst_out_2[11:8] : 4'bz;  // Controlled_Buffer controlled_buffer_2
  or or_8 (or_8_out, decoder_2_out0, out_26);
  assign out_17 = decoder_2_out0 ? instructuon_register_1_inst_out[5:4] : 2'bz;  // Controlled_Buffer controlled_buffer_3
  assign out_19 = decoder_2_out0 ? instructuon_register_1_inst_out[1:0] : 2'bz;  // Controlled_Buffer controlled_buffer_4
  assign out_25 = decoder_2_out3 ? instructuon_register_1_inst_out : 8'bz;  // Controlled_Buffer controlled_buffer_5
  assign out_27 = out_26 ? instructuon_register_1_inst_out : 8'bz;  // Controlled_Buffer controlled_buffer_6
  or or_9 (or_9_out, decoder_2_out0, out_26);
  or or_10 (or_10_out, out_30, out_29);
  not not_1 (not_1_out, out_22);
  or or_11 (out_14, decoder_2_out2, out_20);
  Multiplexer #(.select(2), .enable("false")) multiplexer_1 (
    .in1(1'b0), .in2(1'b1), .out(out_18), .sel({out_20, out_22}));  // open: in0, in3
  or or_12 (or_12_out, or_10_out, out_31);
  assign out_28 = and_14_out ? instructuon_register_1_inst_out : 8'bz;  // Controlled_Buffer controlled_buffer_7
  or or_13 (or_13_out, or_12_out, out_32);
  or or_14 (out_16, decoder_2_out1, out_22);
  or or_15 (or_15_out, out_20, out_22);
  D_Flip_Flop d_ff_1 (.D(and_13_out), .clk(in_3), .Q(out_24), .reset(or_16_out));  // open: Qn, preset
  and and_13 (and_13_out, or_9_out, in_5);
  and and_14 (and_14_out, or_13_out, not_1_out);
  D_Flip_Flop d_ff_2 (.D(or_15_out), .clk(in_3), .Q(d_ff_2_q), .reset(or_18_out));  // open: Qn, preset
  or or_16 (or_16_out, in_5, in_4);
  or or_17 (out_21, out_22, d_ff_2_q);
  or or_18 (or_18_out, in_2, in_4);
endmodule

module Arithmetic_Logic_Unit (
  input  in_1,
  input  in_2,
  input  [7:0] in_3,
  input  [7:0] in_4,
  input  in_5,
  input  [3:0] in_6,
  output out_7,
  output out_8,
  output out_9,
  output out_10,
  output out_11,
  output [7:0] out_12,
  output out_13
);

  wire adder_1_cout, comparator_1_eq, comparator_1_gt, comparator_1_lt, nor_2_out, nor_3_out, nor_4_out,
       nor_5_out, nor_6_out, nor_7_out, nor_8_out, subtractor_1_bout;
  wire [7:0] adder_1_out, adder_2_out, and_1_out, multiplexer_1_out, nand_1_out, negator_1_out, nor_1_out,
       not_1_out, or_1_out, shifter_1_out, subtractor_1_out, subtractor_2_out, xor_1_out;

  Adder adder_1 (.a(in_3), .b(in_4), .out(adder_1_out), .cin(in_1), .cout(adder_1_cout));
  Subtractor subtractor_1 (.a(in_3), .b(in_4), .out(subtractor_1_out), .bin(in_2), .bout(subtractor_1_bout));
  assign not_1_out = ~in_3;  // NOT_Gate not_1, 8 bits wide
  Negator negator_1 (.in(in_3), .out(negator_1_out));
  Shifter shifter_1 (.in(in_3), .\dist (in_4[2:0]), .out(shifter_1_out));
  assign and_1_out = in_3 & in_4;  // AND_Gate and_1, 8 bits wide
  assign or_1_out = in_3 | in_4;  // OR_Gate or_1, 8 bits wide
  assign nand_1_out = ~(in_3 & in_4);  // NAND_Gate nand_1, 8 bits wide
  assign nor_1_out = ~(in_3 | in_4);  // NOR_Gate nor_1, 8 bits wide
  assign xor_1_out = in_3 ^ in_4;  // XOR_Gate xor_1, 8 bits wide
  Adder adder_2 (.a(in_3), .b(8'h1), .out(adder_2_out), .cin(1'b0));  // open: cout
  Subtractor subtractor_2 (.a(in_3), .b(8'h1), .out(subtractor_2_out), .bin(1'b0));  // open: bout
  Multiplexer #(.select(4), .width(8), .enable("false")) multiplexer_1 (
    .in0(adder_1_out), .in1(subtractor_1_out), .in2(negator_1_out), .in3(shifter_1_out), .in4(not_1_out),
    .in5(and_1_out), .in6(or_1_out), .in7(nand_1_out), .in8(nor_1_out), .in9(xor_1_out), .in10(adder_2_out),
    .in11(subtractor_2_out), .out(multiplexer_1_out), .sel(in_6));  // open: in12, in13, in14, in15
  assign out_7 = in_5 ? adder_1_cout : 1'bz;  // Controlled_Buffer controlled_buffer_1
  assign out_8 = in_5 ? subtractor_1_bout : 1'bz;  // Controlled_Buffer controlled_buffer_2
  assign out_12 = in_5 ? multiplexer_1_out : 8'bz;  // Controlled_Buffer controlled_buffer_3
  nor nor_2 (nor_2_out, multiplexer_1_out[7], multiplexer_1_out[6]);
  nor nor_3 (nor_3_out, nor_2_out, multiplexer_1_out[5]);
  nor nor_4 (nor_4_out, nor_3_out, multiplexer_1_out[4]);
  Comparator comparator_1 (.a(in_3), .b(in_4), .gt(comparator_1_gt), .eq(comparator_1_eq), .lt(comparator_1_lt));
  nor nor_5 (nor_5_out, nor_4_out, multiplexer_1_out[3]);
  nor nor_6 (nor_6_out, nor_5_out, multiplexer_1_out[2]);
  nor nor_7 (nor_7_out, nor_6_out, multiplexer_1_out[1]);
  nor nor_8 (nor_8_out, nor_7_out, multiplexer_1_out[0]);
  assign out_9 = in_5 ? comparator_1_gt : 1'bz;  // Controlled_Buffer controlled_buffer_4
  assign out_10 = in_5 ? comparator_1_eq : 1'bz;  // Controlled_Buffer controlled_buffer_5
  assign out_11 = in_5 ? comparator_1_lt : 1'bz;  // Controlled_Buffer controlled_buffer_6
  assign out_13 = in_5 ? nor_8_out : 1'bz;  // Controlled_Buffer controlled_buffer_7
endmodule

module Flag_Register (
  input  [5:0] DATA_IN,
  input  WRT,
  input  CLK,
  input  RST,
  input  READ,
  output [5:0] DATA_OUT
);

  wire [5:0] register_1_q;

  Register #(.width(6)) register_1 (.D(DATA_IN), .en(WRT), .clk(CLK), .Q(register_1_q), .clr(RST));
  assign DATA_OUT = READ ? register_1_q : 6'bz;  // Controlled_Buffer controlled_buffer_1
endmodule

module Stack_Pointer (
  input  in_1,
  input  in_2,
  input  in_3,
  input  in_4,
  output [7:0] out_5
);

  wire [7:0] adder_1_out, counter_1_q;

  Counter counter_1 (.clr(in_1), .load(1'b0), .up(in_2), .clk(in_3), .Q(counter_1_q));  // open: count, D, carry
  Adder adder_1 (.a(counter_1_q), .b(8'h80), .out(adder_1_out), .cin(1'b0));  // open: cout
  assign out_5 = in_4 ? adder_1_out : 8'bz;  // Controlled_Buffer controlled_buffer_1
endmodule

module Program_Pointer (
  input  [7:0] DATA_IN,
  input  WRT,
  input  CLK,
  input  RST,
  input  READ,
  output [7:0] DATA_OUT
);

  wire [7:0] register_1_q;

  Register register_1 (.D(DATA_IN), .en(WRT), .clk(CLK), .Q(register_1_q), .clr(RST));
  assign DATA_OUT = READ ? register_1_q : 8'bz;  // Controlled_Buffer controlled_buffer_1
endmodule
